# Fritzing sketch optocoupler_switch (saved by Fritzing 0.9.0b)
breadboards: 1

parts:
  Raspberry_Pi1 = Raspberry Pi B rev2
  LED1 = LED - 5mm [color="White (6500K)" package="5 mm [THT]"]
  LED2 = LED - 5mm [color="White (6500K)" package="5 mm [THT]"]
  R1 = Resistor [tolerance=±5% resistance=100 package=THT]
  R2 = Resistor [tolerance=±5% resistance=100 package=THT]
  R3 = Photocell (LDR) [package=THT]
  R4 = Photocell (LDR) [package=THT]

nets:
  N1: Raspberry_Pi1.GPIO_23, R2.Pin_0
  N2: Raspberry_Pi1.GPIO_25, R1.Pin_1
  N3: Raspberry_Pi1.GND, LED1.cathode, LED2.cathode
  N4: LED1.anode, R2.Pin_1
  N5: LED2.anode, R1.Pin_0
  N6: R3.pin_0, R4.pin_1

notes:
  Release wire
  Ground wire
  Focus wire
